// Digital circuit 01-Exam.dig as structural Verilog
module _01_Exam (
  input  Reset,
  input  Direction,
  input  Clock,
  output A,
  output B
);

  QPE_DiagramBased qpe_diagrambased_1 (.Reset(Reset), .Direction(Direction), .Clock(Clock), .X(A), .Y(B));
endmodule

/* Test case 01Exam-Test:
# Test vectors for Quadrature Phase Encoding
# Finite State Machine
Reset Clock Direction A B
1     0     0	      0 0
0     0     0         0 0
0     1     0         0 1
0     0     0         0 1
0     1     0         1 1
0     0     0         1 1
0     1     0         1 0
0     0     0         1 0
0     1     0         0 0
# Change to CCW direction
1     0     1         0 0
0     0     1         0 0 
0     1     1         1 0
0     0     1         1 0
0     1     1         1 1
0     0     1         1 1
0     1     1         0 1
0     0     1         0 1
0     1     1         0 0
*/
