// Digital circuit QuadraturePhaseEncoder.dig as structural Verilog
module QuadraturePhaseEncoder (
  input  Reset,
  input  Direction,
  input  Clock,
  output A,
  output B
);

  wire and_1_out, and_2_out, and_3_out, and_4_out, not_1_out, not_2_out, not_3_out, or_1_out, or_2_out;

  not not_1 (not_1_out, Direction);
  not not_2 (not_2_out, A);
  not not_3 (not_3_out, B);
  and and_1 (and_1_out, Direction, not_3_out);
  and and_2 (and_2_out, not_1_out, B);
  and and_3 (and_3_out, not_1_out, not_2_out);
  and and_4 (and_4_out, Direction, A);
  or or_1 (or_1_out, and_1_out, and_2_out);
  or or_2 (or_2_out, and_3_out, and_4_out);
  D_FF_AS Z_1_n (.Set(1'b0), .D(or_1_out), .C(Clock), .Clr(Reset), .Q(A));  // open: nQ
  D_FF_AS Z_0_n (.Set(1'b0), .D(or_2_out), .C(Clock), .Clr(Reset), .Q(B));  // open: nQ
  // Probe state on {A, B}

  // Other names for the same wires on the sheet: Z_0_n = B; Z_1_n = A

  // Notes on the sheet:
  //   Clock: Hz: 2
endmodule
