// Digital circuit QPE-DiagramBased.dig as structural Verilog
module QPE_DiagramBased (
  input  Reset,
  input  Direction,
  input  Clock,
  output X,
  output Y
);

  wire and_1_out, and_2_out, and_3_out, and_4_out, not_1_out, not_2_out, not_3_out, or_1_out, or_2_out;

  not not_1 (not_1_out, Direction);
  not not_2 (not_2_out, X);
  not not_3 (not_3_out, Y);
  and and_1 (and_1_out, Direction, not_3_out);
  and and_2 (and_2_out, not_1_out, Y);
  and and_3 (and_3_out, not_1_out, not_2_out);
  and and_4 (and_4_out, Direction, X);
  or or_1 (or_1_out, and_1_out, and_2_out);
  or or_2 (or_2_out, and_3_out, and_4_out);
  D_FF_AS Z_1_n (.Set(1'b0), .D(or_1_out), .C(Clock), .Clr(Reset), .Q(X));  // open: nQ
  D_FF_AS Z_0_n (.Set(1'b0), .D(or_2_out), .C(Clock), .Clr(Reset), .Q(Y));  // open: nQ
  // Probe state on {X, Y}

  // Other names for the same wires on the sheet: Z_0_n = Y; Z_1_n = X

  // Notes on the sheet:
  //   Clock: Hz: 2
endmodule
