// Digital circuit PushbuttonLEDCircuitDiagramBased.dig as structural Verilog
module PushbuttonLEDCircuitDiagramBased (
  input  Pushbutton,
  input  C,
  output BlueLED,
  output OrangeLED
);

  wire and_1_out, and_2_out, and_3_out, and_4_out, and_5_out, and_6_out, and_7_out, not_1_out, not_2_out,
       not_3_out, not_4_out, or_1_out, or_2_out, Z_0_n;

  not not_1 (not_1_out, Pushbutton);
  not not_2 (not_2_out, BlueLED);
  not not_3 (not_3_out, OrangeLED);
  not not_4 (not_4_out, Z_0_n);
  and and_1 (and_1_out, not_1_out, Z_0_n, OrangeLED, not_2_out);
  and and_2 (and_2_out, Pushbutton, BlueLED);
  and and_3 (and_3_out, not_4_out, BlueLED);
  and and_4 (and_4_out, not_3_out, BlueLED);
  and and_5 (and_5_out, not_1_out, Z_0_n, not_3_out);
  and and_6 (and_6_out, Pushbutton, OrangeLED);
  and and_7 (and_7_out, not_4_out, OrangeLED);
  or or_1 (or_1_out, and_5_out, and_6_out, and_7_out);
  or or_2 (or_2_out, and_1_out, and_2_out, and_3_out, and_4_out);
  D_FF Z_2_n (.D(or_2_out), .C(C), .Q(BlueLED));  // open: nQ
  D_FF Z_1_n (.D(or_1_out), .C(C), .Q(OrangeLED));  // open: nQ
  D_FF u_Z_0_n (.D(Pushbutton), .C(C), .Q(Z_0_n));  // open: nQ
  // Probe 02ExamDiagram.fsm on {BlueLED, OrangeLED, Z_0_n}

  // Other names for the same wires on the sheet: Z_1_n = OrangeLED; Z_2_n = BlueLED

  // Notes on the sheet:
  //   C: Hz: 2
endmodule
