// Digital circuit 02Exam.dig as structural Verilog
module _02Exam (
  input  Pushbutton,
  input  Clock
);

  wire pushbuttonledcircuitdiagrambased_1_blueled, pushbuttonledcircuitdiagrambased_1_orangeled;

  PushbuttonLEDCircuitDiagramBased pushbuttonledcircuitdiagrambased_1 (
    .Pushbutton(Pushbutton), .C(Clock), .BlueLED(pushbuttonledcircuitdiagrambased_1_blueled),
    .OrangeLED(pushbuttonledcircuitdiagrambased_1_orangeled));
  LED BlueLED (.in(pushbuttonledcircuitdiagrambased_1_blueled));
  LED OrangeLED (.in(pushbuttonledcircuitdiagrambased_1_orangeled));
endmodule

/* Test case:
# Test vectors for 02Exam (Push Button)
Clock Pushbutton BlueLED OrangeLED
0     0          0	 0
1     0		 0	 0
0     1		 0	 0
1     1		 0	 0
0     1		 0	 0
1     1		 0	 0
0     0		 0	 0
1     0		 0	 1
0     0		 0	 1
1     0		 0	 1
0     1		 0	 1
1     1		 0	 1
0     0		 0	 1
1     0		 1	 0
0     1		 1	 0
1     1		 1	 0
0     0		 1	 0
1     0		 1	 1
0     1		 1	 1
1     1		 1	 1
0     0		 1	 1
1     0		 0	 0
*/
