// Digital circuit ALU.dig as structural Verilog
module ALU (
  input  [7:0] P,
  input  [7:0] Q,
  input  F0,
  input  F1,
  output [7:0] fPQ,
  output Z
);

  wire [7:0] Add_s, Dec_s, Inc_s, Sub_s;

  Comparator #(.Bits(8)) comparator_1 (.a(fPQ), .b({8{1'b0}}), .eq(Z));  // open: gt, lt
  Add #(.Bits(8)) Add (.a(P), .b(Q), .c_i(1'b0), .s(Add_s));  // open: c_o
  Sub #(.Bits(8)) Sub (.a(P), .b(Q), .c_i(1'b0), .s(Sub_s));  // open: c_o
  Add #(.Bits(8)) Inc (.a(Q), .b(8'h1), .c_i(1'b0), .s(Inc_s));  // open: c_o
  Sub #(.Bits(8)) Dec (.a(Q), .b(8'h1), .c_i(1'b0), .s(Dec_s));  // open: c_o
  Multiplexer #(.Selector_Bits(2), .Bits(8)) multiplexer_1 (
    .sel({F1, F0}), .in_0(Add_s), .in_1(Sub_s), .in_2(Inc_s), .in_3(Dec_s), .out(fPQ));

  // Other names for the same wires on the sheet: F1F0Local[1:0] = {F1, F0}; FPQLocal[7:0] = fPQ; PLocal[7:0] = P;
  //   QLocal[7:0] = Q
endmodule
