// Digital circuit SimpleCPUTestbench.dig as structural Verilog
module SimpleCPUTestbench (
  input  Clock,
  input  Reset,
  output [4:0] AddressBus,
  output [2:0] Opcode,
  output Z,
  output [7:0] DataBus
);

  wire and_1_out, clg_solution_1_calu, clg_solution_1_cd0, clg_solution_1_cir, clg_solution_1_cmar,
       clg_solution_1_cmbr, clg_solution_1_cpc, clg_solution_1_ealu, clg_solution_1_ed0, clg_solution_1_eir,
       clg_solution_1_embr, clg_solution_1_epc, clg_solution_1_f0, clg_solution_1_f1,
       instructionsequencerfsm_1_execute, instructionsequencerfsm_1_t0, instructionsequencerfsm_1_t1,
       instructionsequencerfsm_1_t2, instructionsequencerfsm_1_t3, instructionsequencerfsm_1_t4,
       instructionsequencerfsm_1_t5, instructionsequencerfsm_1_t6, instructionsequencerfsm_1_t7, not_1_out,
       opcodedecoder_1_add, opcodedecoder_1_beq, opcodedecoder_1_bra, opcodedecoder_1_dec,
       opcodedecoder_1_inc, opcodedecoder_1_load, opcodedecoder_1_store, opcodedecoder_1_sub, ReadLocal,
       WriteLocal;

  InstructionSequencerFSM instructionsequencerfsm_1 (
    .Opcode(Opcode), .Clock(Clock), .T0(instructionsequencerfsm_1_t0), .T1(instructionsequencerfsm_1_t1),
    .T2(instructionsequencerfsm_1_t2), .T3(instructionsequencerfsm_1_t3), .T4(instructionsequencerfsm_1_t4),
    .T5(instructionsequencerfsm_1_t5), .T6(instructionsequencerfsm_1_t6), .T7(instructionsequencerfsm_1_t7),
    .Execute(instructionsequencerfsm_1_execute));
  OpcodeDecoder opcodedecoder_1 (
    .Opcode(Opcode), .Execute(instructionsequencerfsm_1_execute), .Load(opcodedecoder_1_load),
    .Store(opcodedecoder_1_store), .Add(opcodedecoder_1_add), .Sub(opcodedecoder_1_sub),
    .Inc(opcodedecoder_1_inc), .Dec(opcodedecoder_1_dec), .Bra(opcodedecoder_1_bra), .Beq(opcodedecoder_1_beq));
  and and_1 (and_1_out, WriteLocal, ~Clock);  // And
  not not_1 (not_1_out, Reset);
  CLG_Solution clg_solution_1 (
    .Reset(Reset), .Clock(Clock), .Load(opcodedecoder_1_load), .Store(opcodedecoder_1_store),
    .Add(opcodedecoder_1_add), .Sub(opcodedecoder_1_sub), .Inc(opcodedecoder_1_inc),
    .Dec(opcodedecoder_1_dec), .Bra(opcodedecoder_1_bra), .Beq(opcodedecoder_1_beq),
    .T0(instructionsequencerfsm_1_t0), .T1(instructionsequencerfsm_1_t1), .T2(instructionsequencerfsm_1_t2),
    .T3(instructionsequencerfsm_1_t3), .T4(instructionsequencerfsm_1_t4), .T5(instructionsequencerfsm_1_t5),
    .T6(instructionsequencerfsm_1_t6), .T7(instructionsequencerfsm_1_t7), .Z(Z), .Read(ReadLocal),
    .Write(WriteLocal), .Cmar(clg_solution_1_cmar), .Cmbr(clg_solution_1_cmbr), .Embr(clg_solution_1_embr),
    .Cir(clg_solution_1_cir), .Eir(clg_solution_1_eir), .Cpc(clg_solution_1_cpc), .Epc(clg_solution_1_epc),
    .Cd0(clg_solution_1_cd0), .Ed0(clg_solution_1_ed0), .Calu(clg_solution_1_calu),
    .Ealu(clg_solution_1_ealu), .F0(clg_solution_1_f0), .F1(clg_solution_1_f1));
  EEPROM #(.AddrBits(5), .Bits(8)) ProgramDataMemory (
    .A(AddressBus), .CS(not_1_out), .WE(and_1_out), .OE(ReadLocal), .D(DataBus));
  Seven_Seg_Hex seven_seg_hex_1 (.d({3'b000, AddressBus[4]}), .dp(1'b0));
  Seven_Seg_Hex seven_seg_hex_2 (.d(AddressBus[3:0]), .dp(1'b0));
  Datapath datapath_1 (
    .Clock(Clock), .DataBus(DataBus), .Cmar(clg_solution_1_cmar), .Cmbr(clg_solution_1_cmbr),
    .Embr(clg_solution_1_embr), .Cir(clg_solution_1_cir), .Eir(clg_solution_1_eir), .Cpc(clg_solution_1_cpc),
    .Epc(clg_solution_1_epc), .Cd0(clg_solution_1_cd0), .Ed0(clg_solution_1_ed0), .Calu(clg_solution_1_calu),
    .Ealu(clg_solution_1_ealu), .F0(clg_solution_1_f0), .F1(clg_solution_1_f1), .AddressBus(AddressBus),
    .Opcode(Opcode), .Z(Z));
  Seven_Seg_Hex seven_seg_hex_3 (.d(DataBus[7:4]), .dp(1'b0));
  Seven_Seg_Hex seven_seg_hex_4 (.d(DataBus[3:0]), .dp(1'b0));

  // Other names for the same wires on the sheet: AddressBusLocal[4:0] = AddressBus; ClockLocal = Clock;
  //   DataBusLocal[7:0] = DataBus; OpcodeLocal[2:0] = Opcode; ResetLocal = Reset; ZLocal = Z

  // Notes on the sheet:
  //   Clock: Hz: 2147483647
  //   contents of ProgramDataMemory (hex, n*v repeats v):
  //   9,4a,6b,29,89,a9,e8,c0,c8,0,1,2
endmodule
