// Digital circuit AddressDecoder.dig as structural Verilog
module AddressDecoder (
  input  [4:0] AddressBus,
  output CS0,
  output CS1
);

  Comparator #(.Bits(5)) comparator_1 (.a(AddressBus), .b({5{1'b1}}), .eq(CS0));  // open: gt, lt
  not not_1 (CS1, CS0);
endmodule
