// Digital circuit AdvancedCPUTestBench.dig as structural Verilog
module AdvancedCPUTestBench (
  input  Clock,
  input  Reset
);

  wire not_1_out, simplecpu_1_read, simplecpu_1_write;
  wire [4:0] simplecpu_1_addressbus;
  wire [7:0] ProgramDataMemory_d;

  SimpleCPU simplecpu_1 (
    .Clock(Clock), .Reset(Reset), .DataBus(ProgramDataMemory_d), .AddressBus(simplecpu_1_addressbus),
    .Write(simplecpu_1_write), .Read(simplecpu_1_read));
  not not_1 (not_1_out, Reset);
  EEPROM #(.AddrBits(5), .Bits(8)) ProgramDataMemory (
    .A(simplecpu_1_addressbus), .CS(not_1_out), .WE(simplecpu_1_write), .OE(simplecpu_1_read),
    .D(ProgramDataMemory_d));

  // Notes on the sheet:
  //   Clock: Hz: 5
  //   contents of ProgramDataMemory (hex, n*v repeats v):
  //   19,53,33,19,55,35,d3,13,79,33,15,79,35,b9,f0,c0,18,39,c0,b9,f7,99,e7,d7,6,6
endmodule
