// Digital circuit CLG-Solution.dig as structural Verilog
module CLG_Solution (
  input  Reset,
  input  Clock,
  input  Load,
  input  Store,
  input  Add,
  input  Sub,
  input  Inc,
  input  Dec,
  input  Bra,
  input  Beq,
  input  T0,
  input  T1,
  input  T2,
  input  T3,
  input  T4,
  input  T5,
  input  T6,
  input  T7,
  input  Z,
  output Read,
  output Write,
  output Cmar,
  output Cmbr,
  output Embr,
  output Cir,
  output Eir,
  output Cpc,
  output Epc,
  output Cd0,
  output Ed0,
  output Calu,
  output Ealu,
  output F0,
  output F1
);

  wire and_1_out, and_2_out, and_3_out, and_4_out, and_5_out, and_6_out, and_7_out, and_8_out, and_9_out,
       and_10_out, and_11_out, and_12_out, and_13_out, and_14_out, and_15_out, and_16_out, and_17_out,
       and_18_out, and_19_out, and_20_out, and_21_out, and_22_out, and_23_out, and_24_out, and_25_out,
       and_26_out, and_27_out, and_28_out, and_29_out, and_30_out, and_31_out, and_32_out, and_33_out,
       zlatched_1_zlatched;

  ZLatched zlatched_1 (
    .Z(Z), .Clock(Clock), .T6(T6), .Add(Add), .Sub(Sub), .Inc(Inc), .Dec(Dec), .ZLatched(zlatched_1_zlatched));
  and and_1 (and_1_out, T5, Add);
  and and_2 (and_2_out, T5, Sub);
  and and_3 (and_3_out, T5, Inc);
  and and_4 (and_4_out, T5, Dec);
  and and_5 (and_5_out, T6, Add);
  and and_6 (and_6_out, T6, Sub);
  and and_7 (and_7_out, T6, Inc);
  and and_8 (and_8_out, T6, Dec);
  and and_9 (and_9_out, T4, Bra);
  and and_10 (and_10_out, T4, zlatched_1_zlatched, Beq);
  and and_11 (and_11_out, Load, T5);
  and and_12 (and_12_out, Add, T5);
  and and_13 (and_13_out, Sub, T5);
  and and_14 (and_14_out, Inc, T5);
  and and_15 (and_15_out, Dec, T5);
  and and_16 (and_16_out, T5, Store);
  and and_17 (and_17_out, Inc, T7);
  and and_18 (and_18_out, T7, Dec);
  or or_1 (Cmar, T0, T4);
  or or_2 (Embr, and_5_out, and_6_out, and_7_out, and_8_out);
  or or_3 (Cmbr, and_1_out, and_2_out, and_3_out, and_4_out);
  or or_4 (Cpc, T3, and_9_out, and_10_out);
  or or_5 (Read, T1, and_11_out, and_12_out, and_13_out, and_14_out, and_15_out);
  or or_6 (Write, and_16_out, and_17_out, and_18_out);
  or or_7 (Epc, T0, T2);
  and and_19 (and_19_out, T5, Load);
  and and_20 (and_20_out, T7, Add);
  and and_21 (and_21_out, T7, Sub);
  or or_8 (Cd0, and_19_out, and_20_out, and_21_out);
  and and_22 (and_22_out, T6, Add);
  and and_23 (and_23_out, T6, Sub);
  and and_24 (and_24_out, T6, Inc);
  and and_25 (and_25_out, T6, Dec);
  and and_26 (and_26_out, T7, Add);
  and and_27 (and_27_out, T7, Sub);
  and and_28 (and_28_out, T7, Inc);
  and and_29 (and_29_out, T7, Dec);
  and and_30 (and_30_out, T6, Inc);
  and and_31 (and_31_out, T6, Dec);
  and and_32 (and_32_out, T6, Sub);
  and and_33 (and_33_out, T6, Dec);
  and and_34 (Ed0, T5, Store);
  or or_9 (F0, and_32_out, and_33_out);
  or or_10 (Calu, T2, and_22_out, and_23_out, and_24_out, and_25_out);
  or or_11 (Ealu, T3, and_26_out, and_27_out, and_28_out, and_29_out);
  or or_12 (F1, T2, and_30_out, and_31_out);

  assign Cir = T1;
  assign Eir = T4;

  // Other names for the same wires on the sheet: AddLocal = Add; BeqLocal = Beq; BraLocal = Bra; ClockLocal = Clock;
  //   DecLocal = Dec; IncLocal = Inc; LoadLocal = Load; StoreLocal = Store; SubLocal = Sub; T0Local = T0;
  //   T1Local = T1; T2Local = T2; T3Local = T3; T4Local = T4; T5Local = T5; T6Local = T6; T7Local = T7; ZLocal = Z
endmodule
