// Digital circuit ZLatched.dig as structural Verilog
module ZLatched (
  input  Z,
  input  Clock,
  input  T6,
  input  Add,
  input  Sub,
  input  Inc,
  input  Dec,
  output ZLatched
);

  wire and_1_out, and_2_out, and_3_out, and_4_out, and_5_out, or_1_out;

  and and_1 (and_1_out, T6, Add);
  and and_2 (and_2_out, T6, Sub);
  and and_3 (and_3_out, T6, Inc);
  and and_4 (and_4_out, T6, Dec);
  or or_1 (or_1_out, and_1_out, and_2_out, and_3_out, and_4_out);
  and and_5 (and_5_out, or_1_out, ~Clock);  // And
  D_FF d_ff_1 (.D(Z), .C(and_5_out), .Q(ZLatched));  // open: nQ

  // Other names for the same wires on the sheet: AddLocal = Add; ClockLocal = Clock; DecLocal = Dec; IncLocal = Inc;
  //   SubLocal = Sub; T6Local = T6; ZLocal = Z
endmodule
