// Digital circuit AdvancedCPUTestBenchPortRegister.dig as structural Verilog
module AdvancedCPUTestBenchPortRegister (
  input  Clock,
  input  Reset
);

  wire addressdecoder_1_cs0, addressdecoder_1_cs1, simplecpu_1_read, simplecpu_1_write;
  wire [4:0] simplecpu_1_addressbus;
  wire [7:0] portregister_1_dataout, ProgramDataMemory_d;

  SimpleCPU simplecpu_1 (
    .Clock(Clock), .Reset(Reset), .DataBus(ProgramDataMemory_d), .AddressBus(simplecpu_1_addressbus),
    .Write(simplecpu_1_write), .Read(simplecpu_1_read));
  AddressDecoder addressdecoder_1 (
    .AddressBus(simplecpu_1_addressbus), .CS0(addressdecoder_1_cs0), .CS1(addressdecoder_1_cs1));
  EEPROM #(.AddrBits(5), .Bits(8)) ProgramDataMemory (
    .A(simplecpu_1_addressbus), .CS(addressdecoder_1_cs1), .WE(simplecpu_1_write), .OE(simplecpu_1_read),
    .D(ProgramDataMemory_d));
  PortRegister portregister_1 (
    .Write(simplecpu_1_write), .Read(simplecpu_1_read), .CS(addressdecoder_1_cs0),
    .DataBus(ProgramDataMemory_d), .DataOut(portregister_1_dataout));
  Seven_Seg_Hex seven_seg_hex_1 (.d(portregister_1_dataout[3:0]), .dp(1'b0));
  Seven_Seg_Hex seven_seg_hex_2 (.d(portregister_1_dataout[7:4]), .dp(1'b0));

  // Notes on the sheet:
  //   Clock: Hz: 5
  //   contents of ProgramDataMemory (hex, n*v repeats v):
  //   19,53,33,19,55,35,d3,13,79,33,15,79,35,b9,f0,c0,18,39,c0,b9,f7,99,e7,d7,6,6
endmodule
