// Digital circuit ControlUnit.dig as structural Verilog
module ControlUnit (
  input  Clock,
  input  Reset,
  input  [2:0] Opcode,
  input  Z,
  output Read,
  output Write,
  output Cmar,
  output Cmbr,
  output Embr,
  output Cir,
  output Eir,
  output Cpc,
  output Epc,
  output Cd0,
  output Ed0,
  output Calu,
  output Ealu,
  output F0,
  output F1
);

  wire instructionsequencerfsm_1_execute, instructionsequencerfsm_1_t0, instructionsequencerfsm_1_t1,
       instructionsequencerfsm_1_t2, instructionsequencerfsm_1_t3, instructionsequencerfsm_1_t4,
       instructionsequencerfsm_1_t5, instructionsequencerfsm_1_t6, instructionsequencerfsm_1_t7,
       opcodedecoder_1_add, opcodedecoder_1_beq, opcodedecoder_1_bra, opcodedecoder_1_dec,
       opcodedecoder_1_inc, opcodedecoder_1_load, opcodedecoder_1_store, opcodedecoder_1_sub;

  OpcodeDecoder opcodedecoder_1 (
    .Opcode(Opcode), .Execute(instructionsequencerfsm_1_execute), .Load(opcodedecoder_1_load),
    .Store(opcodedecoder_1_store), .Add(opcodedecoder_1_add), .Sub(opcodedecoder_1_sub),
    .Inc(opcodedecoder_1_inc), .Dec(opcodedecoder_1_dec), .Bra(opcodedecoder_1_bra), .Beq(opcodedecoder_1_beq));
  InstructionSequencerFSM instructionsequencerfsm_1 (
    .Opcode(Opcode), .Clock(Clock), .T0(instructionsequencerfsm_1_t0), .T1(instructionsequencerfsm_1_t1),
    .T2(instructionsequencerfsm_1_t2), .T3(instructionsequencerfsm_1_t3), .T4(instructionsequencerfsm_1_t4),
    .T5(instructionsequencerfsm_1_t5), .T6(instructionsequencerfsm_1_t6), .T7(instructionsequencerfsm_1_t7),
    .Execute(instructionsequencerfsm_1_execute));
  CLG_Solution clg_solution_1 (
    .Reset(Reset), .Clock(Clock), .Load(opcodedecoder_1_load), .Store(opcodedecoder_1_store),
    .Add(opcodedecoder_1_add), .Sub(opcodedecoder_1_sub), .Inc(opcodedecoder_1_inc),
    .Dec(opcodedecoder_1_dec), .Bra(opcodedecoder_1_bra), .Beq(opcodedecoder_1_beq),
    .T0(instructionsequencerfsm_1_t0), .T1(instructionsequencerfsm_1_t1), .T2(instructionsequencerfsm_1_t2),
    .T3(instructionsequencerfsm_1_t3), .T4(instructionsequencerfsm_1_t4), .T5(instructionsequencerfsm_1_t5),
    .T6(instructionsequencerfsm_1_t6), .T7(instructionsequencerfsm_1_t7), .Z(Z), .Read(Read), .Write(Write),
    .Cmar(Cmar), .Cmbr(Cmbr), .Embr(Embr), .Cir(Cir), .Eir(Eir), .Cpc(Cpc), .Epc(Epc), .Cd0(Cd0), .Ed0(Ed0),
    .Calu(Calu), .Ealu(Ealu), .F0(F0), .F1(F1));
endmodule
