// Digital circuit Datapath.dig as structural Verilog
module Datapath (
  input  Clock,
  input  [7:0] DataBus,
  input  Cmar,
  input  Cmbr,
  input  Embr,
  input  Cir,
  input  Eir,
  input  Cpc,
  input  Epc,
  input  Cd0,
  input  Ed0,
  input  Calu,
  input  Ealu,
  input  F0,
  input  F1,
  output [4:0] AddressBus,
  output [2:0] Opcode,
  output Z
);

  wire [4:0] IR_q;
  wire [7:0] alu_1_fpq, ALUregister_q, D0_q, MBR_q, PC_q;
  wire [7:5] MAR_q;

  Register #(.Bits(8)) MAR (.D(DataBus), .C(Clock), .en(Cmar), .Q({MAR_q, AddressBus}));
  Register #(.Bits(8)) MBR (.D(DataBus), .C(Clock), .en(Cmbr), .Q(MBR_q));
  Register #(.Bits(8)) IR (.D(DataBus), .C(Clock), .en(Cir), .Q({Opcode, IR_q}));
  Register #(.Bits(8)) PC (.D(DataBus), .C(Clock), .en(Cpc), .Q(PC_q));
  Register #(.Bits(8)) D0 (.D(DataBus), .C(Clock), .en(Cd0), .Q(D0_q));
  assign DataBus = Embr ? MBR_q : 8'bz;  // Driver driver_1
  assign DataBus = Eir ? {Opcode, IR_q} : 8'bz;  // Driver driver_2
  assign DataBus = Epc ? PC_q : 8'bz;  // Driver driver_3
  assign DataBus = Ed0 ? D0_q : 8'bz;  // Driver driver_4
  ALU alu_1 (.P(D0_q), .Q(DataBus), .F0(F0), .F1(F1), .fPQ(alu_1_fpq), .Z(Z));
  Register #(.Bits(8)) ALUregister (.D(alu_1_fpq), .C(Clock), .en(Calu), .Q(ALUregister_q));
  assign DataBus = Ealu ? ALUregister_q : 8'bz;  // Driver driver_5

  // Other names for the same wires on the sheet: CaluLocal = Calu; Cd0Local = Cd0; CirLocal = Cir; ClockLocal = Clock;
  //   CmarLocal = Cmar; CmbrLocal = Cmbr; CpcLocal = Cpc; DataBusLocal[7:0] = DataBus; EaluLocal = Ealu;
  //   Ed0Local = Ed0; EirLocal = Eir; EmbrLocal = Embr; EpcLocal = Epc; F0Local = F0; F1Local = F1
endmodule
