// Digital circuit PortRegister.dig as structural Verilog
module PortRegister (
  input  Write,
  input  Read,
  input  CS,
  input  [7:0] DataBus,
  output [7:0] DataOut
);

  wire and_1_out;

  and and_1 (and_1_out, CS, Read);
  Register #(.Bits(8)) _0x31 (.D(DataBus), .C(Write), .en(CS), .Q(DataOut));
  assign DataBus = and_1_out ? DataOut : 8'bz;  // Driver driver_1

  // Other names for the same wires on the sheet: CSLocal = CS; ReadLocal = Read
endmodule
