// Digital circuit SimpleCPU.dig as structural Verilog
module SimpleCPU (
  input  Clock,
  input  Reset,
  input  [7:0] DataBus,
  output [4:0] AddressBus,
  output Write,
  output Read
);

  wire controlunit_1_calu, controlunit_1_cd0, controlunit_1_cir, controlunit_1_cmar, controlunit_1_cmbr,
       controlunit_1_cpc, controlunit_1_ealu, controlunit_1_ed0, controlunit_1_eir, controlunit_1_embr,
       controlunit_1_epc, controlunit_1_f0, controlunit_1_f1, controlunit_1_write, datapath_1_z;
  wire [2:0] datapath_1_opcode;

  ControlUnit controlunit_1 (
    .Clock(Clock), .Reset(Reset), .Opcode(datapath_1_opcode), .Z(datapath_1_z), .Read(Read),
    .Write(controlunit_1_write), .Cmar(controlunit_1_cmar), .Cmbr(controlunit_1_cmbr),
    .Embr(controlunit_1_embr), .Cir(controlunit_1_cir), .Eir(controlunit_1_eir), .Cpc(controlunit_1_cpc),
    .Epc(controlunit_1_epc), .Cd0(controlunit_1_cd0), .Ed0(controlunit_1_ed0), .Calu(controlunit_1_calu),
    .Ealu(controlunit_1_ealu), .F0(controlunit_1_f0), .F1(controlunit_1_f1));
  Datapath datapath_1 (
    .Clock(Clock), .DataBus(DataBus), .Cmar(controlunit_1_cmar), .Cmbr(controlunit_1_cmbr),
    .Embr(controlunit_1_embr), .Cir(controlunit_1_cir), .Eir(controlunit_1_eir), .Cpc(controlunit_1_cpc),
    .Epc(controlunit_1_epc), .Cd0(controlunit_1_cd0), .Ed0(controlunit_1_ed0), .Calu(controlunit_1_calu),
    .Ealu(controlunit_1_ealu), .F0(controlunit_1_f0), .F1(controlunit_1_f1), .AddressBus(AddressBus),
    .Opcode(datapath_1_opcode), .Z(datapath_1_z));
  and and_1 (Write, controlunit_1_write, ~Clock);  // And
endmodule
