// Digital circuit OpcodeDecoder.dig as structural Verilog
module OpcodeDecoder (
  input  [2:0] Opcode,
  input  Execute,
  output Load,
  output Store,
  output Add,
  output Sub,
  output Inc,
  output Dec,
  output Bra,
  output Beq
);

  and and_1 (Load, ~Opcode[2], ~Opcode[1], ~Opcode[0], Execute);  // And
  and and_2 (Store, ~Opcode[2], ~Opcode[1], Opcode[0], Execute);  // And
  and and_3 (Add, ~Opcode[2], Opcode[1], ~Opcode[0], Execute);  // And
  and and_4 (Sub, ~Opcode[2], Opcode[1], Opcode[0], Execute);  // And
  and and_5 (Inc, Opcode[2], ~Opcode[1], ~Opcode[0], Execute);  // And
  and and_6 (Dec, Opcode[2], ~Opcode[1], Opcode[0], Execute);  // And
  and and_7 (Bra, Opcode[2], Opcode[1], ~Opcode[0], Execute);  // And
  and and_8 (Beq, Opcode[2], Opcode[1], Opcode[0], Execute);

  // Notes on the sheet:
  //   Add: Addition
  //   Sub: Subtract
  //   Inc: Increment
  //   Dec: Decrement
  //   Bra: Branch
  //   Beq: Branch if equal
endmodule
