// Digital circuit SimpleCPUTestbench.dig as structural Verilog
module SimpleCPUTestbench (
  input  Clock,
  input  Reset,
  output [4:0] AddressBus,
  output [2:0] Opcode,
  output Z,
  output [7:0] DataBus
);

  wire and_1_out, controlsignalslogic_1_calu, controlsignalslogic_1_cd0, controlsignalslogic_1_cir,
       controlsignalslogic_1_cmar, controlsignalslogic_1_cmbr, controlsignalslogic_1_cpc,
       controlsignalslogic_1_ealu, controlsignalslogic_1_ed0, controlsignalslogic_1_eir,
       controlsignalslogic_1_embr, controlsignalslogic_1_epc, controlsignalslogic_1_f0,
       controlsignalslogic_1_f1, instructionsequencerfsm_1_execute, instructionsequencerfsm_1_t0,
       instructionsequencerfsm_1_t1, instructionsequencerfsm_1_t2, instructionsequencerfsm_1_t3,
       instructionsequencerfsm_1_t4, instructionsequencerfsm_1_t5, instructionsequencerfsm_1_t6,
       instructionsequencerfsm_1_t7, not_1_out, opcodedecoder_1_add, opcodedecoder_1_beq,
       opcodedecoder_1_bra, opcodedecoder_1_dec, opcodedecoder_1_inc, opcodedecoder_1_load,
       opcodedecoder_1_store, opcodedecoder_1_sub, ReadLocal, WriteLocal;
  wire [0:0] undriven;

  InstructionSequencerFSM instructionsequencerfsm_1 (
    .Opcode(Opcode), .Clock(Clock), .T0(instructionsequencerfsm_1_t0), .T1(instructionsequencerfsm_1_t1),
    .T2(instructionsequencerfsm_1_t2), .T3(instructionsequencerfsm_1_t3), .T4(instructionsequencerfsm_1_t4),
    .T5(instructionsequencerfsm_1_t5), .T6(instructionsequencerfsm_1_t6), .T7(instructionsequencerfsm_1_t7),
    .Execute(instructionsequencerfsm_1_execute));
  OpcodeDecoder opcodedecoder_1 (
    .Opcode(Opcode), .Execute(instructionsequencerfsm_1_execute), .Load(opcodedecoder_1_load),
    .Store(opcodedecoder_1_store), .Add(opcodedecoder_1_add), .Sub(opcodedecoder_1_sub),
    .Inc(opcodedecoder_1_inc), .Dec(opcodedecoder_1_dec), .Bra(opcodedecoder_1_bra), .Beq(opcodedecoder_1_beq));
  and and_1 (and_1_out, WriteLocal, ~Clock);  // And
  not not_1 (not_1_out, Reset);
  ControlSignalsLogic controlsignalslogic_1 (
    .Reset(Reset), .Clock(Clock), .Load(opcodedecoder_1_load), .Store(opcodedecoder_1_store),
    .Add(opcodedecoder_1_add), .Sub(opcodedecoder_1_sub), .Inc(opcodedecoder_1_inc),
    .Dec(opcodedecoder_1_dec), .Bra(opcodedecoder_1_bra), .Beq(opcodedecoder_1_beq),
    .T0(instructionsequencerfsm_1_t0), .T1(instructionsequencerfsm_1_t1), .T2(instructionsequencerfsm_1_t2),
    .T3(instructionsequencerfsm_1_t3), .T4(instructionsequencerfsm_1_t4), .T5(instructionsequencerfsm_1_t5),
    .T6(instructionsequencerfsm_1_t6), .T7(instructionsequencerfsm_1_t7), .Z(Z), .Read(ReadLocal),
    .Write(WriteLocal), .Cmar(controlsignalslogic_1_cmar), .Cmbr(controlsignalslogic_1_cmbr),
    .Embr(controlsignalslogic_1_embr), .Cir(controlsignalslogic_1_cir), .Eir(controlsignalslogic_1_eir),
    .Cpc(controlsignalslogic_1_cpc), .Epc(controlsignalslogic_1_epc), .Cd0(controlsignalslogic_1_cd0),
    .Ed0(controlsignalslogic_1_ed0), .Calu(controlsignalslogic_1_calu), .Ealu(controlsignalslogic_1_ealu),
    .F0(controlsignalslogic_1_f0), .F1(controlsignalslogic_1_f1));
  EEPROM ProgramDataMemory (.A(AddressBus[1:0]), .CS(not_1_out), .WE(and_1_out), .OE(ReadLocal), .D(DataBus[0]));
  Seven_Seg_Hex seven_seg_hex_1 (.d({3'b000, undriven[0]}), .dp(1'b0));
  Datapath datapath_1 (
    .Clock(Clock), .DataBus(DataBus), .Cmar(controlsignalslogic_1_cmar), .Cmbr(controlsignalslogic_1_cmbr),
    .Embr(controlsignalslogic_1_embr), .Cir(controlsignalslogic_1_cir), .Eir(controlsignalslogic_1_eir),
    .Cpc(controlsignalslogic_1_cpc), .Epc(controlsignalslogic_1_epc), .Cd0(controlsignalslogic_1_cd0),
    .Ed0(controlsignalslogic_1_ed0), .Calu(controlsignalslogic_1_calu), .Ealu(controlsignalslogic_1_ealu),
    .F0(controlsignalslogic_1_f0), .F1(controlsignalslogic_1_f1), .AddressBus(AddressBus), .Opcode(Opcode),
    .Z(Z));
  Seven_Seg_Hex seven_seg_hex_2 (.d(AddressBus[3:0]), .dp(1'b0));
  Seven_Seg_Hex seven_seg_hex_3 (.d(DataBus[7:4]), .dp(1'b0));
  Seven_Seg_Hex seven_seg_hex_4 (.d(DataBus[3:0]), .dp(1'b0));
  // Pins of 1 and 8 bits meet at DataBus
  // Pins of 2 and 4 and 5 bits meet at AddressBus

  // Other names for the same wires on the sheet: AddressBusLocal[4:0] = AddressBus; ClockLocal = Clock;
  //   DataBusLocal[7:0] = DataBus; OpcodeLocal[2:0] = Opcode; ResetLocal = Reset; ZLocal = Z
endmodule
