// Digital circuit OpcodeDecoderTestBench.dig as structural Verilog
module OpcodeDecoderTestBench (
  input  [2:0] Opcode,
  input  Execute,
  output Load,
  output Store,
  output Add,
  output Sub,
  output Inc,
  output Dec,
  output Bra,
  output Beq
);

  OpcodeDecoder opcodedecoder_1 (
    .Opcode(Opcode), .Execute(Execute), .Load(Load), .Store(Store), .Add(Add), .Sub(Sub), .Inc(Inc),
    .Dec(Dec), .Bra(Bra), .Beq(Beq));
endmodule

/* Test case:
# Test vectors for opcode decoder
# Inputs: Opcode (3 bits), Execute
# Outputs: Load, Store, Add, Sub, Inc, Dec, Bra, Beq
# When Execute = 0, all outputs equal 0
# When Execute = 1, decode Opcode
Opcode 	Execute Load 	Store 	Add 	Sub 	Inc 	Dec 	Bra 	Beq
# Load instruction
0	0	0	0	0	0	0	0	0	0
0	1	1	0	0	0	0	0	0	0
#Store instruction
1	0	0	0	0	0	0	0	0	0
1	1	0	1	0	0	0	0	0	0
# Add instruction
2	0	0	0	0	0	0	0	0	0
2	1	0	0	1	0	0	0	0	0
# Subtract instruction
3	0	0	0	0	0	0	0	0	0
3	1	0	0	0	1	0	0	0	0
# Increment instruction
4	0	0	0	0	0	0	0	0	0
4	1	0	0	0	0	1	0	0	0
# Decrement instruction
5	0	0	0	0	0	0	0	0	0
5	1	0	0	0	0	0	1	0	0
# Branch instruction
6	0	0	0	0	0	0	0	0	0
6	1	0	0	0	0	0	0	1	0
# Branch if equal to zero instruction
7	0	0	0	0	0	0	0	0	0
7	1	0	0	0	0	0	0	0	1
*/
