// Digital circuit ControlSignalsLogic.dig as structural Verilog
module ControlSignalsLogic (
  input  Reset,
  input  Clock,
  input  Load,
  input  Store,
  input  Add,
  input  Sub,
  input  Inc,
  input  Dec,
  input  Bra,
  input  Beq,
  input  T0,
  input  T1,
  input  T2,
  input  T3,
  input  T4,
  input  T5,
  input  T6,
  input  T7,
  input  Z,
  output Read,
  output Write,
  output Cmar,
  output Cmbr,
  output Embr,
  output Cir,
  output Eir,
  output Cpc,
  output Epc,
  output Cd0,
  output Ed0,
  output Calu,
  output Ealu,
  output F0,
  output F1
);

  wire and_2_out, and_3_out, and_4_out, and_5_out, and_6_out, and_7_out, and_8_out, and_9_out, and_10_out,
       and_11_out, and_12_out, and_13_out, and_14_out, and_15_out, and_16_out, and_17_out, and_18_out,
       and_19_out, and_20_out, and_21_out, and_22_out, and_23_out, and_24_out, and_25_out, and_26_out,
       and_27_out, and_28_out, and_29_out, and_30_out, and_31_out, and_32_out, and_33_out, and_34_out,
       and_35_out, and_36_out, and_37_out, and_38_out, and_39_out, and_40_out, and_41_out, and_42_out,
       and_43_out, and_44_out, and_45_out, and_46_out, and_47_out, and_48_out, BeqLocal, zlatched_1_zlatched;

  ZLatched zlatched_1 (
    .Z(Z), .Clock(Clock), .T6(T6), .Add(Add), .Sub(Sub), .Inc(Inc), .Dec(Dec), .ZLatched(zlatched_1_zlatched));
  and and_1 (BeqLocal, Beq, zlatched_1_zlatched);
  and and_2 (and_2_out, T4, Load);
  and and_3 (and_3_out, T4, Store);
  and and_4 (and_4_out, T4, Add);
  and and_5 (and_5_out, T4, Sub);
  and and_6 (and_6_out, T4, Inc);
  and and_7 (and_7_out, T4, Dec);
  and and_8 (and_8_out, T5, Add);
  and and_9 (and_9_out, T5, Sub);
  and and_10 (and_10_out, T5, Inc);
  and and_11 (and_11_out, T5, Dec);
  and and_12 (and_12_out, T6, Add);
  and and_13 (and_13_out, T6, Sub);
  and and_14 (and_14_out, T6, Inc);
  and and_15 (and_15_out, T6, Dec);
  and and_16 (and_16_out, Load, T5);
  and and_17 (and_17_out, Add, T5);
  and and_18 (and_18_out, Sub, T5);
  and and_19 (and_19_out, Inc, T5);
  and and_20 (and_20_out, Dec, T5);
  and and_21 (and_21_out, T5, Store);
  and and_22 (and_22_out, Inc, T7);
  and and_23 (and_23_out, T7, Dec);
  or or_1 (Cmbr, and_8_out, and_9_out, and_10_out, and_11_out);
  or or_2 (Embr, and_12_out, and_13_out, and_14_out, and_15_out);
  or or_3 (Read, T1, and_16_out, and_17_out, and_18_out, and_19_out, and_20_out);
  or or_4 (Write, and_21_out, and_22_out, and_23_out);
  or or_5 (Cmar, T0, and_2_out, and_3_out, and_4_out, and_5_out, and_6_out, and_7_out);
  and and_24 (and_24_out, T4, Load);
  and and_25 (and_25_out, T4, Store);
  and and_26 (and_26_out, T4, Add);
  and and_27 (and_27_out, T4, Sub);
  and and_28 (and_28_out, T4, Inc);
  and and_29 (and_29_out, T4, Dec);
  and and_30 (and_30_out, T4, Bra);
  and and_31 (and_31_out, T4, BeqLocal);
  and and_32 (and_32_out, T4, Bra);
  and and_33 (and_33_out, T4, BeqLocal);
  or or_6 (Epc, T0, T2);
  and and_34 (and_34_out, T5, Load);
  and and_35 (and_35_out, T7, Add);
  and and_36 (and_36_out, T7, Sub);
  or or_7 (Eir, and_24_out, and_25_out, and_26_out, and_27_out, and_28_out, and_29_out, and_30_out, and_31_out);
  or or_8 (Cd0, and_34_out, and_35_out, and_36_out);
  or or_9 (Cpc, T3, and_32_out, and_33_out);
  and and_37 (and_37_out, T6, Add);
  and and_38 (and_38_out, T6, Sub);
  and and_39 (and_39_out, T6, Inc);
  and and_40 (and_40_out, T6, Dec);
  and and_41 (and_41_out, T7, Add);
  and and_42 (and_42_out, T7, Sub);
  and and_43 (and_43_out, T7, Inc);
  and and_44 (and_44_out, T7, Dec);
  and and_45 (and_45_out, T6, Inc);
  and and_46 (and_46_out, T6, Dec);
  and and_47 (and_47_out, T6, Sub);
  and and_48 (and_48_out, T6, Dec);
  and and_49 (Ed0, T5, Store);
  or or_10 (F0, and_47_out, and_48_out);
  or or_11 (Calu, T2, and_37_out, and_38_out, and_39_out, and_40_out);
  or or_12 (Ealu, T3, and_41_out, and_42_out, and_43_out, and_44_out);
  or or_13 (F1, T2, and_45_out, and_46_out);

  assign Cir = T1;

  // Other names for the same wires on the sheet: AddLocal = Add; BraLocal = Bra; ClockLocal = Clock; DecLocal = Dec;
  //   IncLocal = Inc; LoadLocal = Load; StoreLocal = Store; SubLocal = Sub; T0Local = T0; T1Local = T1; T2Local = T2;
  //   T3Local = T3; T4Local = T4; T5Local = T5; T6Local = T6; T7Local = T7; ZLocal = Z
endmodule
