// Digital circuit InstructionSequencerFSM.dig as structural Verilog
module InstructionSequencerFSM (
  input  [2:0] Opcode,
  input  Clock,
  output T0,
  output T1,
  output T2,
  output T3,
  output T4,
  output T5,
  output T6,
  output T7,
  output Execute
);

  wire and_1_out, and_2_out, and_3_out, and_4_out, and_5_out, and_6_out, and_7_out, not_1_out, not_2_out,
       not_3_out, not_4_out, not_5_out, or_1_out, or_2_out, or_3_out, Q_0_n, Q_1_n;

  not not_1 (not_1_out, Opcode[2]);
  not not_2 (not_2_out, Opcode[1]);
  not not_3 (not_3_out, Execute);
  not not_4 (not_4_out, Q_1_n);
  not not_5 (not_5_out, Q_0_n);
  and and_1 (and_1_out, Q_0_n, Q_1_n);
  and and_2 (and_2_out, not_2_out, not_1_out, Q_0_n);
  and and_3 (and_3_out, Opcode[1], Opcode[2]);
  and and_4 (and_4_out, Q_0_n, Q_1_n);
  and and_5 (and_5_out, Opcode[1], Q_0_n);
  and and_6 (and_6_out, Opcode[2], Q_0_n);
  and and_7 (and_7_out, Q_0_n, not_3_out);
  or or_1 (or_1_out, not_2_out, not_1_out, not_3_out);
  and and_8 (T0, not_5_out, not_4_out, not_3_out);
  and and_9 (T1, Q_0_n, not_4_out, not_3_out);
  and and_10 (T2, not_5_out, Q_1_n, not_3_out);
  and and_11 (T3, Q_0_n, Q_1_n, not_3_out);
  and and_12 (T4, not_5_out, not_4_out, Execute);
  and and_13 (T5, Q_0_n, not_4_out, Execute);
  and and_14 (T6, not_5_out, Q_1_n, Execute);
  and and_15 (T7, Q_0_n, Q_1_n, Execute);
  or or_2 (or_2_out, and_2_out, and_3_out, and_4_out);
  or or_3 (or_3_out, and_5_out, and_6_out, and_7_out);
  JK_FF Q_2_n (.J(and_1_out), .C(Clock), .K(or_2_out), .Q(Execute));  // open: nQ
  JK_FF u_Q_1_n (.J(or_3_out), .C(Clock), .K(Q_0_n), .Q(Q_1_n));  // open: nQ
  JK_FF u_Q_0_n (.J(or_1_out), .C(Clock), .K(1'b1), .Q(Q_0_n));  // open: nQ

  // Other names for the same wires on the sheet: Q_2_n = Execute

  // Notes on the sheet:
  //   Clock: Hz: 2
endmodule
