// Digital circuit InstructionSequencerFSMTestbench.dig as structural Verilog
module InstructionSequencerFSMTestbench (
  input  [2:0] Opcode,
  input  Clock,
  output Execute,
  output T0,
  output T1,
  output T2,
  output T3,
  output T4,
  output T5,
  output T6,
  output T7
);

  InstructionSequencerFSM instructionsequencerfsm_1 (
    .Opcode(Opcode), .Clock(Clock), .T0(T0), .T1(T1), .T2(T2), .T3(T3), .T4(T4), .T5(T5), .T6(T6), .T7(T7),
    .Execute(Execute));
endmodule

/* Test case:
# Test vectors for control signals logic
Clock Opcode T0 T1 T2 T3 T4 T5 T6 T7 Execute
# Load instruction
# MAR ← [PC]
0     0      1  0  0  0  0  0  0  0  0
# IR ← [MAR]
1     0      0  1  0  0  0  0  0  0  0
0     0      0  1  0  0  0  0  0  0  0
# ALU (Q) ← [PC]
1     0      0  0  1  0  0  0  0  0  0
0     0      0  0  1  0  0  0  0  0  0
# PC ← [ALU]
1     0      0  0  0  1  0  0  0  0  0
0     0      0  0  0  1  0  0  0  0  0
# MAR ← [IR]
1     0      0  0  0  0  1  0  0  0  1
0     0      0  0  0  0  1  0  0  0  1
# D0 ← [MAR]
1     0      0  0  0  0  0  1  0  0  1
0     0      0  0  0  0  0  1  0  0  1
# Store instruction
# MAR ← [PC]
1     0      1  0  0  0  0  0  0  0  0
0     0      1  0  0  0  0  0  0  0  0
# IR ← [MAR]
1     0      0  1  0  0  0  0  0  0  0
0     0      0  1  0  0  0  0  0  0  0
# ALU (Q) ← [PC]
1     0      0  0  1  0  0  0  0  0  0
0     0      0  0  1  0  0  0  0  0  0
# PC ← [ALU]
1     0      0  0  0  1  0  0  0  0  0
0     0      0  0  0  1  0  0  0  0  0
# MAR ← [IR]
1     1      0  0  0  0  1  0  0  0  1
0     1      0  0  0  0  1  0  0  0  1
# [MAR] ← [D0]
1     1      0  0  0  0  0  1  0  0  1
0     1      0  0  0  0  0  1  0  0  1
# Add instruction
# MAR ← [PC]
1     0      1  0  0  0  0  0  0  0  0
0     0      1  0  0  0  0  0  0  0  0
# IR ← [MAR]
1     0      0  1  0  0  0  0  0  0  0
0     0      0  1  0  0  0  0  0  0  0
# ALU (Q) ← [PC]
1     0      0  0  1  0  0  0  0  0  0
0     0      0  0  1  0  0  0  0  0  0
# PC ← [ALU]
1     0      0  0  0  1  0  0  0  0  0
0     0      0  0  0  1  0  0  0  0  0
# MAR ← [IR]
1     2      0  0  0  0  1  0  0  0  1
0     2      0  0  0  0  1  0  0  0  1
# MBR ← [MAR]
1     2      0  0  0  0  0  1  0  0  1
0     2      0  0  0  0  0  1  0  0  1
# ALU (P) ← [MBR]
1     2      0  0  0  0  0  0  1  0  1
0     2      0  0  0  0  0  0  1  0  1
# D0 ← [ALU]
1     2      0  0  0  0  0  0  0  1  1
0     2      0  0  0  0  0  0  0  1  1
# Sub instruction
# MAR ← [PC]
1     0      1  0  0  0  0  0  0  0  0
0     0      1  0  0  0  0  0  0  0  0
# IR ← [MAR]
1     0      0  1  0  0  0  0  0  0  0
0     0      0  1  0  0  0  0  0  0  0
# ALU (Q) ← [PC]
1     0      0  0  1  0  0  0  0  0  0
0     0      0  0  1  0  0  0  0  0  0
# PC ← [ALU]
1     0      0  0  0  1  0  0  0  0  0
0     0      0  0  0  1  0  0  0  0  0
# MAR ← [IR]
1     3      0  0  0  0  1  0  0  0  1
0     3      0  0  0  0  1  0  0  0  1
# MBR ← [MAR]
1     3      0  0  0  0  0  1  0  0  1
0     3      0  0  0  0  0  1  0  0  1
# ALU (P) ← [MBR]
1     3      0  0  0  0  0  0  1  0  1
0     3      0  0  0  0  0  0  1  0  1
# D0 ← [ALU]
1     3      0  0  0  0  0  0  0  1  1
0     3      0  0  0  0  0  0  0  1  1
# Inc instruction
# MAR ← [PC]
1     0      1  0  0  0  0  0  0  0  0
0     0      1  0  0  0  0  0  0  0  0
# IR ← [MAR]
1     0      0  1  0  0  0  0  0  0  0
0     0      0  1  0  0  0  0  0  0  0
# ALU (Q) ← [PC]
1     0      0  0  1  0  0  0  0  0  0
0     0      0  0  1  0  0  0  0  0  0
# PC ← [ALU]
1     0      0  0  0  1  0  0  0  0  0
0     0      0  0  0  1  0  0  0  0  0
# MAR ← [IR]
1     4      0  0  0  0  1  0  0  0  1
0     4      0  0  0  0  1  0  0  0  1
# MBR ← [MAR]
1     4      0  0  0  0  0  1  0  0  1
0     4      0  0  0  0  0  1  0  0  1
# ALU (P) ← [MBR]
1     4      0  0  0  0  0  0  1  0  1
0     4      0  0  0  0  0  0  1  0  1
# D0 ← [ALU]
1     4      0  0  0  0  0  0  0  1  1
0     4      0  0  0  0  0  0  0  1  1
# Dec instruction
# MAR ← [PC]
1     0      1  0  0  0  0  0  0  0  0
0     0      1  0  0  0  0  0  0  0  0
# IR ← [MAR]
1     0      0  1  0  0  0  0  0  0  0
0     0      0  1  0  0  0  0  0  0  0
# ALU (Q) ← [PC]
1     0      0  0  1  0  0  0  0  0  0
0     0      0  0  1  0  0  0  0  0  0
# PC ← [ALU]
1     0      0  0  0  1  0  0  0  0  0
0     0      0  0  0  1  0  0  0  0  0
# MAR ← [IR]
1     5      0  0  0  0  1  0  0  0  1
0     5      0  0  0  0  1  0  0  0  1
# MBR ← [MAR]
1     5      0  0  0  0  0  1  0  0  1
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*/
